# Fritzing sketch GaragePi (saved by Fritzing 0.9.2b)
breadboards: 2

parts:
  DHT1 = DHT22 Humidity and Temperature Sensor [part_number=DHT22]
  J1 = Cobbler Plus
  Power_plug1 = Power plug
  IC1 = Voltage Regulator [part_number=LM7805 package=to220-igo]
  D1 = Rectifier Diode [part_number=1N4007 package="300 mil [THT]"]  # not connected
  C1 = Electrolytic Capacitor [capacitance=0.47mF package="100 mil [THT, electrolytic]"]
  C2 = Electrolytic Capacitor [capacitance=1µF package="100 mil [THT, electrolytic]"]  # not connected
  R1 = Resistor [tolerance=±5% resistance=10k package=THT]
  U1 = HALL-EFFECT [package=sc70]
  LED1 = smd LED [color="Red (633nm)" package="0603 [SMD]"]  # not connected
  Q1 = TRANSISTOR_NPN [package=to-92]
  R2 = Resistor [tolerance=±5% resistance=220 package=THT]
  R3 = Resistor [tolerance=±5% resistance=220 package=THT]

nets:
  VDD: DHT1.VDD, IC1.OUT, R1.Pin_1, U1.VCC
  N1: DHT1.DATA, J1.CE1, R1.Pin_0
  GND: DHT1.GND, J1.GND, Power_plug1.GND, IC1.IN, C1.+, U1.GND, R3.Pin_0
  N2: J1.#6, U1.OUT
  N3: J1.#16, R2.Pin_0
  N4: IC1.GND, C1.-
  N5: Q1.E, R3.Pin_1
  N6: Q1.B, R2.Pin_1

notes:
  Ambient T/H
  5V Regulator (VDD)
  12VDC Supply (VCC)
  GPIO is 3V3
  Window Module
  Base Station

custom parts:
  Cobbler Plus: The Cobbler Plus is an add on prototyping board from Adafruit specifically designed for the Raspberry Pi B+ that can break out all those tasty power, GPIO, I2C and SPI pins from the 40-pin header onto a solderless breadboard. This set will make "cobbling together" prototypes with the Pi super easy. The Cobbler Plus can plug into any solderless breadboard.
