# Fritzing sketch GaragePiDuino (saved by Fritzing 0.9.2b)
circuit board: 6.37352cm x 4.60492cm

parts:
  12VDC = Power plug
  D1 = Rectifier Diode [part_number=1N4004 package="300 mil [THT]"]
  12V_LED = LED - 5mm [color="Green (560nm)" package="5 mm [THT]"]
  5V_LED = LED - 5mm [color="Red (633nm)" package="5 mm [THT]"]
  C1 = Electrolytic Capacitor [capacitance=0.1mF package="100 mil [THT, electrolytic]"]
  C2 = Electrolytic Capacitor [capacitance=10µF package="100 mil [THT, electrolytic]"]
  IC1 = Voltage Regulator [package=to220-igo]
  R1 = Resistor [tolerance=±5% resistance=1k package=THT]
  R2 = Resistor [tolerance=±5% resistance=470 package=THT]
  Lux_Sensor_0V_5V_SIG = male pin header, 3 pins [form="♂ (male)"]
  Relay_5V_0V_IN1_IN2_IN3_IN4 = male pin header, 6 pins [form="♂ (male)"]
  T/H_0V_SIG_5V = male pin header, 3 pins [form="♂ (male)"]
  HALL1_0V_5V_SIG = male pin header, 3 pins [form="♂ (male)"]
  HALL2_0V_5V_SIG = male pin header, 3 pins [form="♂ (male)"]
  LED_STRIP_1A = Power plug
  Relay_1_NC = male pin header, 2 pins [form="♂ (male)"]

nets:
  GND: 12VDC.GND, 12V_LED.cathode, 5V_LED.cathode, C1.-, C2.-, IC1.GND, Lux_Sensor_0V_5V_SIG.pin1, Relay_5V_0V_IN1_IN2_IN3_IN4.pin2, T/H_0V_SIG_5V.pin1, HALL1_0V_5V_SIG.pin1, HALL2_0V_5V_SIG.pin1, LED_STRIP_1A.GND
  N1: 12VDC.VCC, D1.anode, R1.Pin_0
  N2: D1.cathode, C1.+, IC1.IN, Relay_1_NC.pin1
  N3: 12V_LED.anode, R1.Pin_1
  N4: 5V_LED.anode, R2.Pin_0
  N5: C2.+, IC1.OUT, R2.Pin_1, Lux_Sensor_0V_5V_SIG.pin2, Relay_5V_0V_IN1_IN2_IN3_IN4.pin1, T/H_0V_SIG_5V.pin3, HALL1_0V_5V_SIG.pin2, HALL2_0V_5V_SIG.pin2
  N6: LED_STRIP_1A.VCC, Relay_1_NC.pin2
