# Fritzing sketch GarageSensor (saved by Fritzing 0.9.2b)
circuit board: 8.46667cm x 5.64444cm
breadboards: 1

parts:
  Part2 = Arduino Uno (Rev3)
  Part3 = SRF05 Ultrasonic Rangefinder
  R1 = Resistor [tolerance=±5% resistance=560 package=THT]
  R2 = Resistor [tolerance=±5% resistance=560 package=THT]
  LED1 = smd LED [color="Green (570nm)" package="1206 [SMD]"]
  LED2 = smd LED [color="Red (660nm)" package="1206 [SMD]"]

nets:
  N1: Part2.D10_PWM/SS, LED1.anode
  N2: Part2.D11_PWM/MOSI, LED2.anode
  N3: Part2.D12/MISO, Part3.Echo
  N4: Part2.D13/SCK, Part3.Trig
  5V: Part2.5V, Part3.VCC
  GND: Part2.GND, Part3.GND, R1.Pin_1, R2.Pin_1
  N5: R1.Pin_0, LED1.cathode
  N6: R2.Pin_0, LED2.cathode
